# Fritzing sketch fixed_pitch_oscillator (saved by Fritzing 0.9.3b)
circuit board: 7.53753cm x 4.89831cm
breadboards: 1

parts:
  L2 = Inductor [inductance=100µH package="400 mil [THT]"]
  Q1 = NPN-Transistor [package="TO92 [THT]"]
  R2 = Resistor [tolerance=±5% resistance=1k package=THT]
  R3 = Resistor [tolerance=±5% resistance=47k package=THT]
  R4 = Resistor [tolerance=±5% resistance=1k package=THT]
  C4 = Electrolytic Capacitor [capacitance=1µF package="100 mil [THT, electrolytic]"]
  Q3 = NPN-Transistor [package="TO92 [THT]"]
  R5 = Resistor [tolerance=±5% resistance=470 package=THT]
  C6 = Ceramic Capacitor [capacitance=10pF package="100 mil [THT, multilayer]"]
  R6 = Resistor [tolerance=±5% resistance=33 package=THT]
  R7 = Resistor [tolerance=±5% resistance=2.2k package=THT]
  Q4 = NPN-Transistor [package="TO92 [THT]"]
  C7 = Electrolytic Capacitor [capacitance=1µF package="100 mil [THT, electrolytic]"]
  R8 = Resistor [tolerance=±5% resistance=10k package=THT]
  R9 = Resistor [tolerance=±5% resistance=10k package=THT]
  R10 = Resistor [tolerance=±5% resistance=10k package=THT]
  C8 = Electrolytic Capacitor [capacitance=1µF package="100 mil [THT, electrolytic]"]
  C5 = Tantalum Capacitor [capacitance=1µF package="100 mil [THT, tantalum]"]
  C2 = Electrolytic Capacitor [capacitance=10pF package="100 mil [THT, electrolytic]"]
  R11 = Resistor [tolerance=±5% resistance=2.2k package=THT]
  J2 = female pin header, 3 pins [form="♀ (female)"]
  J3 = female pin header, 1 pin [form="♀ (female)"]

nets (from the pcb view):
  N1: L2.pin_0, C4.+, Q3.C, C2.+, J3.pin1
  N2: L2.pin_1, Q1.C, C6.1, Q4.C, C5.+, C2.-
  N3: Q1.E, Q3.E, R11.Pin_1
  N4: Q1.B, R4.Pin_1
  N5: R2.Pin_0, R3.Pin_0, Q3.B
  N6: R2.Pin_1, R4.Pin_0, C4.-, R7.Pin_1, C8.+, J2.pin2
  N7: R3.Pin_1, C5.-
  N8: R5.Pin_0, Q4.B
  N9: R5.Pin_1, C6.0, R6.Pin_0
  N10: R6.Pin_1, R7.Pin_0, C7.+, R10.Pin_1
  N11: Q4.E, C7.-, R8.Pin_0, R9.Pin_0, C8.-
  N12: R8.Pin_1, J2.pin3
  N13: R9.Pin_1, R10.Pin_0, R11.Pin_0, J2.pin1

notes:
  pot
  gnd
  -12V
  +12V
