# Fritzing sketch variable_pitch_oscillator (saved by Fritzing 0.9.3b)
circuit board: 4.62086cm x 5.94028cm
breadboards: 1

parts:
  L2 = Inductor [inductance=100µH package="400 mil [THT]"]
  Q1 = NPN-Transistor [package="TO92 [THT]"]
  R2 = Resistor [tolerance=±5% resistance=1k package=THT]
  R3 = Resistor [tolerance=±5% resistance=47k package=THT]
  R4 = Resistor [tolerance=±5% resistance=1k package=THT]
  C4 = Electrolytic Capacitor [capacitance=1µF package="100 mil [THT, electrolytic]"]
  Q3 = NPN-Transistor [package="TO92 [THT]"]
  C5 = Tantalum Capacitor [capacitance=1µF package="100 mil [THT, tantalum]"]
  C2 = Electrolytic Capacitor [capacitance=10pF package="100 mil [THT, electrolytic]"]
  R5 = Resistor [tolerance=±5% resistance=2.2k package=THT]

nets (from the schematic view):
  N1: L2.pin_0, Q1.C, C5.+, C2.-
  12V: L2.pin_1, C4.+, Q3.C, C2.+
  N2: Q1.E, Q3.E, R5.Pin_0
  N3: Q1.B, R4.Pin_1
  N4: R2.Pin_0, R3.Pin_0, Q3.B
  GND: R2.Pin_1, R4.Pin_0, C4.-
  N5: R3.Pin_1, C5.-
  -12V: R5.Pin_1
