# Fritzing sketch variable_pitch_oscillator_pcb (saved by Fritzing 0.9.3b)
circuit board: 4cm x 5cm
breadboards: 1

parts:
  L2 = Inductor [inductance=100µH package="400 mil [THT]"]
  Q1 = NPN-Transistor [package="TO92 [THT]"]
  R2 = Resistor [tolerance=±5% resistance=1k package=THT]
  R3 = Resistor [tolerance=±5% resistance=47k package=THT]
  R4 = Resistor [tolerance=±5% resistance=1k package=THT]
  Q3 = NPN-Transistor [package="TO92 [THT]"]
  R5 = Resistor [tolerance=±5% resistance=2.2k package=THT]
  C6 = Capacitor [package=0603-cap]
  C4 = Electrolytic Capacitor [capacitance=1µF package="100 mil [THT, electrolytic]"]
  C7 = Capacitor [package=0603-cap]
  J1 = female pin header, 2 pins [form="♀ (female)"]  # not connected
  J2 = female pin header, 1 pin [form="♀ (female)"]  # not connected

nets (from the schematic view):
  N1: L2.pin_0, Q1.C, C6.1, C7.1
  N2: L2.pin_1, C6.2
  N3: Q1.E, Q3.E, R5.Pin_0
  N4: Q1.B, R4.Pin_1
  N5: R2.Pin_0, R3.Pin_0, Q3.B
  GND: R2.Pin_1, R4.Pin_0, C4.-
  N6: R3.Pin_1, C7.2
  12V: Q3.C, C4.+
  -12V: R5.Pin_1

notes:
  gnd
  -12V
  +12V
