# Fritzing sketch volume_oscillator (saved by Fritzing 0.9.3b)
circuit board: 7cm x 5cm
breadboards: 1

parts:
  L2 = Inductor [inductance=68µH package="400 mil [THT]"]
  C2 = Electrolytic Capacitor [capacitance=1pF package="100 mil [THT, electrolytic]"]
  Q1 = NPN-Transistor [package="TO92 [THT]"]
  R4 = Resistor [tolerance=±5% resistance=470 package=THT]
  Q3 = NPN-Transistor [package="TO92 [THT]"]
  R5 = Resistor [tolerance=±5% resistance=470 package=THT]
  C6 = Ceramic Capacitor [capacitance=2.2µF package="100 mil [THT, multilayer]"]
  R6 = Resistor [tolerance=±5% resistance=33 package=THT]
  R7 = Resistor [tolerance=±5% resistance=10k package=THT]
  Q4 = NPN-Transistor [package="TO92 [THT]"]
  C7 = Electrolytic Capacitor [capacitance=1µF package="100 mil [THT, electrolytic]"]
  R9 = Resistor [tolerance=±5% resistance=10k package=THT]
  R10 = Resistor [tolerance=±5% resistance=2.2k package=THT]
  R11 = Resistor [tolerance=±5% resistance=2.2k package=THT]
  C8 = Electrolytic Capacitor [capacitance=1µF package="100 mil [THT, electrolytic]"]
  C10 = Ceramic Capacitor [capacitance=1pF package="100 mil [THT, multilayer]"]
  R12 = Resistor [tolerance=±5% resistance=470 package=THT]
  C11 = Ceramic Capacitor [capacitance=0.22mF package="100 mil [THT, multilayer]"]
  R13 = Resistor [tolerance=±5% resistance=220 package=THT]
  J2 = female pin header, 1 pin [form="♀ (female)"]
  J1 = female pin header, 3 pins [form="♀ (female)"]

nets:
  12V: L2.pin_0, C2.+, Q3.C, J2.pin1
  N1: L2.pin_1, Q1.C, C6.1, Q4.C, C11.0
  GND: C2.-, R4.Pin_0, R10.Pin_1, C8.-, C10.1, R12.Pin_0, J1.pin2
  N2: Q1.E, Q3.E, R13.Pin_0
  N3: Q1.B, R4.Pin_1
  N4: Q3.B, C10.0, R12.Pin_1, C11.1
  N5: R5.Pin_0, Q4.B
  N6: R5.Pin_1, C6.0, R6.Pin_0
  N7: R6.Pin_1, R7.Pin_0, C7.+, R10.Pin_0
  -12V: R7.Pin_1, R9.Pin_1, R13.Pin_1, J1.pin1
  N8: Q4.E, C7.-, R9.Pin_0, R11.Pin_0, C8.+
  N9: R11.Pin_1, J1.pin3

notes:
  to potentiometer
  gnd
  -12V
  +12V
  pot
